# Fritzing sketch Radar (saved by Fritzing 0.9.3b)
breadboards: 1

parts:
  J1 = Basic Servo
  hc-sr1 = hc-sr04
  LED1 = smd LED [color="Green (570nm)" package="0805 [SMD]"]
  Part1 = Arduino Uno (Rev3) - ICSP
  R1 = Resistor [tolerance=±5% resistance=220 package=THT]
  Raspberry_Pi3 = Raspberry Pi 3 [part_number=RPI-3-V1.2]  # not connected
  CONN1 = USB connector [package=THT]
  CONN2 = USB connector [package=THT]
  J2 = T Cobbler Plus  # not connected

nets:
  VCC: J1.vcc, hc-sr1.VCC, Part1.5V
  N1: J1.pulse, Part1.ICSP_MISO, Part1.D12/MISO
  N2: hc-sr1.Trig, Part1.D10_PWM/SS
  N3: hc-sr1.Echo, Part1.D11_PWM/MOSI
  GND: hc-sr1.GND, Part1.GND, R1.Pin_1
  N4: LED1.cathode, R1.Pin_0
  N5: LED1.anode, Part1.D13/SCK
  5V: CONN1.5V, CONN2.5V
  N6: CONN1.d-, CONN2.d-
  N7: CONN1.d+, CONN2.d+
  GND_2: CONN1.GND, CONN1.chassis5, CONN1.chassis6, CONN2.GND, CONN2.chassis5, CONN2.chassis6

custom parts:
  T Cobbler Plus: The T-Cobbler Plus is an add on prototyping board from Adafruit specifically designed for the Raspberry Pi B+ that can break out all those tasty power, GPIO, I2C and SPI pins from the 40-pin header onto a solderless breadboard. This set will make "cobbling together" prototypes with the Pi super easy. The T-Cobbler Plus can plug into any solderless breadboard.
